# Fritzing sketch LCC CAN Physical Interface (saved by Fritzing 0.9.3b)
circuit board: 4.93397cm x 4.69729cm
breadboards: 1

parts:
  R4 = Resistor [tolerance=±5% resistance=47k package=THT]
  R3 = Resistor [tolerance=±5% resistance=47k package=THT]
  R2 = Resistor [tolerance=±20% resistance=100 package=THT]
  Q3 = PNP-Transistor [package="TO92 [THT]"]
  U5 = AD8541 - CMOS Rail-to-Rail Op Amp [part_number=AD8541]
  U6 = AD8541 - CMOS Rail-to-Rail Op Amp [part_number=AD8541]
  R5 = Trimmer Potentiometer [maximum_resistance=10kΩ package=THT]
  U2 = RJ45 Jack [package=rj45-8]
  J1 = Power Jack [package=power_jack_combo]
  JP9 = Header 4 [package=screwterminal-3.5mm-4_lock]
  D7 = Diode [package=diode-1n4001]
  JP10 = Header 4 [package=screwterminal-3.5mm-4_lock]
  D8 = Diode [package=diode-1n4001]
  U1 = RJ45 Jack [package=rj45-8]
  D9 = Diode [package=diode-1n4001]
  R1 = Resistor [tolerance=±20% resistance=0.1 package="0603 [SMD]"]

nets:
  Vin: R4.Pin_0, R2.Pin_0, D8.C, D9.C, R1.Pin_1
  N1: R4.Pin_1, U5.-INA, R5.leg1, R5.wiper
  Vcm: R3.Pin_0, Q3.C, U5.+INA
  GND: R3.Pin_1, R5.leg2, U2.3, U2.6, U2.7, J1.GND, J1.GNDBREAK, JP10.1, U1.3, U1.6, U1.7
  N2: R2.Pin_1, Q3.E, U6.-INA
  N3: Q3.B, U6.OUTA
  Alarm: U5.OUTA, JP10.3
  Vout: U6.+INA, D7.A, R1.Pin_0
  N4: U2.1, JP9.1
  N5: U2.2, JP9.2
  N6: U2.8, D7.C, JP10.2
  N7: J1.PWR, D9.A
  N8: JP9.3, U1.1
  N9: JP9.4, U1.2
  N10: D8.A, U1.8

notes:
  V(R2)=I/(R2/R3)
  Current Monitor
  LCC CAN Physical Interface
  Voltage Comparator for Alarm
  CLo
  CHo
  CLi
  CHi
  GND
  Vo
  Alrm
